// Logisim project Cache(3).circ as structural Verilog: 6 circuits, main circuit implementation
module implementation (
  input  [9:0] CpuAddressIn,
  input  CpuReadIn,
  input  CpuWriteIn,
  input  [7:0] CpuWriteValueIn,
  input  [31:0] LineFromMemIn,
  input  ClkIn,
  output ReadyOut,
  output DidContainOut,
  output [7:0] ByteReadOut,
  output [7:0] MemAddressOut,
  output MemReadOut,
  output MemWriteOut,
  output [31:0] Line2MemOut
);

  wire Age0, Age1, Byte0, Byte1, Contain, Dirty, Initialize, Line0, Line1, NewContain, Set0_contains,
       Set0_dirty, Set1_contains, Set1_dirty;
  wire [6:0] Set0_tag, Set1_tag, StoredTag;
  wire [7:0] Set0_bytereadout, Set1_bytereadout;
  wire [9:0] CpuAddressOut;
  wire [31:0] Set0_line2mem, Set1_line2mem;

  Register #(.width(1)) register_1 (.D(Contain), .en(NewContain), .clk(ClkIn), .Q(DidContainOut));  // open: clr
  Multiplexer #(.enable("false"), .width(8)) multiplexer_1 (
    .in0(CpuAddressOut[9:2]), .in1({StoredTag, CpuAddressOut[2]}), .out(MemAddressOut), .sel(MemWriteOut));
  Controlpath controlpath_1 (
    .CpuAddressIn(CpuAddressIn), .CpuRead(CpuReadIn), .CpuWrite(CpuWriteIn), .Dirty(Dirty),
    .Contain(Contain), .ClkIn(ClkIn), .CpuAddressOut(CpuAddressOut), .Initialize(Initialize),
    .MemWrite(MemWriteOut), .MemRead(MemReadOut), .Age0(Age0), .Age1(Age1), .Line0(Line0), .Line1(Line1),
    .Byte0(Byte0), .Byte1(Byte1), .Ready(ReadyOut), .NewContain(NewContain));
  Set Set0 (
    .LineFromMemIn(LineFromMemIn), .CpuAddressOut(CpuAddressOut), .CpuWriteValueIn(CpuWriteValueIn),
    .Initialize(Initialize), .Ages(Age0), .Ways(Line0), .Byte(Byte0), .ClkIn(ClkIn),
    .Contains(Set0_contains), .ByteReadOut(Set0_bytereadout), .Tag(Set0_tag), .Line2Mem(Set0_line2mem),
    .Dirty(Set0_dirty));
  Set Set1 (
    .LineFromMemIn(LineFromMemIn), .CpuAddressOut(CpuAddressOut), .CpuWriteValueIn(CpuWriteValueIn),
    .Initialize(Initialize), .Ages(Age1), .Ways(Line1), .Byte(Byte1), .ClkIn(ClkIn),
    .Contains(Set1_contains), .ByteReadOut(Set1_bytereadout), .Tag(Set1_tag), .Line2Mem(Set1_line2mem),
    .Dirty(Set1_dirty));
  Multiplexer #(.enable("false")) multiplexer_2 (
    .in0(Set0_contains), .in1(Set1_contains), .out(Contain), .sel(CpuAddressOut[2]));
  Multiplexer #(.enable("false"), .width(8)) multiplexer_3 (
    .in0(Set0_bytereadout), .in1(Set1_bytereadout), .out(ByteReadOut), .sel(CpuAddressOut[2]));
  // Probe on Line2MemOut
  Multiplexer #(.enable("false"), .width(32)) multiplexer_4 (
    .in0(Set0_line2mem), .in1(Set1_line2mem), .out(Line2MemOut), .sel(CpuAddressOut[2]));
  // Probe on StoredTag
  Multiplexer #(.enable("false"), .width(7)) multiplexer_5 (
    .in0(Set0_tag), .in1(Set1_tag), .out(StoredTag), .sel(CpuAddressOut[2]));
  Multiplexer #(.enable("false")) multiplexer_6 (
    .in0(Set0_dirty), .in1(Set1_dirty), .out(Dirty), .sel(CpuAddressOut[2]));
  // Probe on ByteReadOut

  // Other names for the same wires on the sheet: clk = ClkIn; CpuAddress[9:0] = CpuAddressIn;
  //   OffSet[1:0] = CpuAddressOut[1:0]; Sets = CpuAddressOut[2]; Tag[6:0] = CpuAddressOut[9:3]; CpuRead = CpuReadIn;
  //   CpuWrite = CpuWriteIn; CpuWriteValue[7:0] = CpuWriteValueIn; DidContain = DidContainOut;
  //   LineFromMem[31:0] = LineFromMemIn; MemAddress[7:0] = MemAddressOut; MemRead = MemReadOut;
  //   MemWrite = MemWriteOut; Ready = ReadyOut; ByteRead[7:0] = ByteReadOut; SelectedSetByteRead[7:0] = ByteReadOut;
  //   Line2Mem[31:0] = Line2MemOut; SelectedSetLine2Mem[31:0] = Line2MemOut
endmodule

module FSM (
  input  S0,
  input  S1,
  input  S2,
  input  Read,
  input  Write,
  input  Contain,
  input  Dirty,
  output Out0,
  output Out1,
  output Out2,
  output Ready,
  output MemWrite,
  output MemRead,
  output Age,
  output Line,
  output Update,
  output State,
  output Initialize
);

  wire and_1_out, and_2_out, and_3_out, and_4_out, and_5_out, and_6_out, and_7_out, and_8_out, and_9_out,
       and_10_out, and_11_out, and_12_out, and_13_out, and_14_out, and_15_out, and_20_out, and_21_out,
       not_1_out, not_2_out, not_3_out, not_4_out, not_5_out, not_6_out, not_7_out, not_8_out, not_9_out,
       not_10_out, not_11_out, not_12_out, not_13_out, not_14_out, not_15_out, not_16_out, not_17_out,
       not_18_out, not_19_out, not_20_out, not_21_out, not_22_out, not_23_out, not_24_out, not_25_out,
       not_26_out, not_27_out, not_28_out, not_29_out, not_30_out, not_31_out, not_32_out, not_33_out,
       not_34_out, not_35_out, not_36_out, not_37_out, not_38_out, not_39_out, not_40_out, not_41_out,
       not_42_out;

  not not_1 (not_1_out, S2);
  not not_2 (not_2_out, Dirty);
  not not_3 (not_3_out, S2);
  not not_4 (not_4_out, S1);
  not not_5 (not_5_out, S0);
  not not_6 (not_6_out, S1);
  not not_7 (not_7_out, Read);
  not not_8 (not_8_out, S1);
  not not_9 (not_9_out, Read);
  not not_10 (not_10_out, S2);
  not not_11 (not_11_out, S1);
  not not_12 (not_12_out, S2);
  not not_13 (not_13_out, S0);
  not not_14 (not_14_out, Contain);
  not not_15 (not_15_out, S0);
  not not_16 (not_16_out, S1);
  not not_17 (not_17_out, S0);
  not not_18 (not_18_out, S1);
  not not_19 (not_19_out, Read);
  not not_20 (not_20_out, Write);
  not not_21 (not_21_out, S0);
  not not_22 (not_22_out, S0);
  not not_23 (not_23_out, S1);
  not not_24 (not_24_out, Write);
  not not_25 (not_25_out, S0);
  and and_1 (and_1_out, not_1_out, S1, not_2_out);
  and and_2 (and_2_out, not_3_out, S1, Contain);
  and and_3 (and_3_out, S1, S0);
  and and_4 (and_4_out, S2, not_4_out, not_5_out);
  and and_5 (and_5_out, S2, not_6_out, not_7_out);
  and and_6 (and_6_out, not_8_out, S0, not_9_out, Write);
  and and_7 (and_7_out, not_10_out, not_11_out, S0, Read);
  and and_8 (and_8_out, not_12_out, S1, not_13_out, not_14_out, Dirty);
  and and_9 (and_9_out, S2, not_15_out, Read, Write);
  and and_10 (and_10_out, not_16_out, not_17_out);
  and and_11 (and_11_out, not_18_out, not_19_out, not_20_out);
  and and_12 (and_12_out, not_21_out, Dirty);
  and and_13 (and_13_out, not_22_out, Contain);
  and and_14 (and_14_out, S2, not_23_out, not_24_out);
  and and_15 (and_15_out, S2, not_25_out);
  or or_1 (Out2, and_1_out, and_2_out, and_3_out, and_4_out, and_5_out);
  or or_2 (Out1, and_6_out, and_7_out, and_8_out, and_9_out);
  or or_3 (Out0, and_10_out, and_11_out, and_12_out, and_13_out, and_14_out, and_15_out);
  not not_26 (not_26_out, S2);
  not not_27 (not_27_out, S1);
  not not_28 (not_28_out, S0);
  not not_29 (not_29_out, S2);
  not not_30 (not_30_out, S1);
  not not_31 (not_31_out, S2);
  not not_32 (not_32_out, S1);
  not not_33 (not_33_out, S0);
  not not_34 (not_34_out, S2);
  not not_35 (not_35_out, S1);
  not not_36 (not_36_out, S0);
  not not_37 (not_37_out, S1);
  not not_38 (not_38_out, S1);
  not not_39 (not_39_out, S0);
  not not_40 (not_40_out, S0);
  not not_41 (not_41_out, S2);
  not not_42 (not_42_out, S0);
  and and_16 (Initialize, not_26_out, not_27_out, not_28_out);
  and and_17 (Ready, not_29_out, not_30_out, S0);
  and and_18 (MemWrite, not_31_out, S1, S0);
  and and_19 (MemRead, S2, not_32_out, not_33_out);
  and and_20 (and_20_out, not_34_out, not_35_out, not_36_out);
  and and_21 (and_21_out, S2, not_37_out, S0);
  and and_22 (Line, S2, not_38_out, not_39_out);
  and and_23 (Update, S2, S1, not_40_out);
  and and_24 (State, not_41_out, S1, not_42_out);
  or or_4 (Age, and_20_out, and_21_out);
endmodule

module Age (
  input  [1:0] Age0,
  input  [1:0] Age1,
  input  [1:0] Age2,
  input  [1:0] Control,
  output [1:0] OutAge0,
  output [1:0] OutAge1,
  output [1:0] OutAge2
);

  wire [1:0] adder_1_out, adder_2_out, adder_3_out, CurrentAge, Select0, Select1, Select2;

  Adder #(.width(2)) adder_1 (.a(Age0), .b(2'b01), .out(adder_1_out));  // open: cin, cout
  Comparator #(.mode("unsigned"), .width(2)) comparator_1 (
    .a(Age0), .b(CurrentAge), .eq(Select0[0]), .lt(Select0[1]));  // open: gt
  Multiplexer #(.enable("false"), .select(2), .width(2)) multiplexer_1 (
    .in0(Age0), .in1(2'b00), .in2(adder_1_out), .out(OutAge0), .sel(Select0));  // open: in3
  Multiplexer #(.enable("false"), .select(2), .width(2)) multiplexer_2 (
    .in0(Age0), .in1(Age1), .in2(Age2), .out(CurrentAge), .sel(Control));  // open: in3
  Adder #(.width(2)) adder_2 (.a(Age1), .b(2'b01), .out(adder_2_out));  // open: cin, cout
  Comparator #(.mode("unsigned"), .width(2)) comparator_2 (
    .a(Age1), .b(CurrentAge), .eq(Select1[0]), .lt(Select1[1]));  // open: gt
  Multiplexer #(.enable("false"), .select(2), .width(2)) multiplexer_3 (
    .in0(Age1), .in1(2'b00), .in2(adder_2_out), .out(OutAge1), .sel(Select1));  // open: in3
  Adder #(.width(2)) adder_3 (.a(Age2), .b(2'b01), .out(adder_3_out));  // open: cin, cout
  Comparator #(.mode("unsigned"), .width(2)) comparator_3 (
    .a(Age2), .b(CurrentAge), .eq(Select2[0]), .lt(Select2[1]));  // open: gt
  Multiplexer #(.enable("false"), .select(2), .width(2)) multiplexer_4 (
    .in0(Age2), .in1(2'b00), .in2(adder_3_out), .out(OutAge2), .sel(Select2));  // open: in3
endmodule

module Set (
  input  [31:0] LineFromMemIn,
  input  [9:0] CpuAddressOut,
  input  [7:0] CpuWriteValueIn,
  input  Initialize,
  input  Ages,
  input  Ways,
  input  Byte,
  input  ClkIn,
  output Contains,
  output [7:0] ByteReadOut,
  output [6:0] Tag,
  output [31:0] Line2Mem,
  output Dirty
);

  wire and_1_out, Byte0, Byte1, Byte2, comparator_4_eq, comparator_5_eq, comparator_6_eq, Contain0, Contain1,
       Contain2, Dirty0, Dirty1, Dirty2, Is0eldest, Is1eldest, Is2eldest, Valid0, Valid1, Valid2, Way0, Way1,
       Way2;
  wire [1:0] Age0, Age1, Age2, bitfinder_2_index, Index, multiplexer_1_out, multiplexer_4_out,
       multiplexer_5_out, multiplexer_7_out, multiplexer_8_out, NewOutAge0, NewOutAge1, NewOutAge2, OutAge0,
       OutAge1, OutAge2, SelectAge, Selecting;
  wire [2:0] comparator_7_eq;
  wire [6:0] Tag0, Tag1, Tag2;
  wire [7:0] ByteRead0, ByteRead1, ByteRead2;
  wire [31:0] Line2MemOut0, Line2MemOut2;

  Age age_1 (
    .Age0(Age0), .Age1(Age1), .Age2(Age2), .Control(Index), .OutAge0(OutAge0), .OutAge1(OutAge1),
    .OutAge2(OutAge2));
  Way u_Way0 (
    .LineFromMemIn(LineFromMemIn), .CpuAddressOut(CpuAddressOut), .CpuWriteValueIn(CpuWriteValueIn),
    .Initialize(Initialize), .NewAge(Ages), .Line(Way0), .Byte(Byte0), .Age(SelectAge), .ClkIn(ClkIn),
    .Contains(Contain0), .ByteReadOut(ByteRead0), .TagOut(Tag0), .ValidOut(Valid0), .DirtyOut(Dirty0),
    .AgeOut(Age0), .Line2MemOut(Line2MemOut0));
  Way u_Way2 (
    .LineFromMemIn(LineFromMemIn), .CpuAddressOut(CpuAddressOut), .CpuWriteValueIn(CpuWriteValueIn),
    .Initialize(Initialize), .NewAge(Ages), .Line(Way2), .Byte(Byte2), .Age(SelectAge), .ClkIn(ClkIn),
    .Contains(Contain2), .ByteReadOut(ByteRead2), .TagOut(Tag2), .ValidOut(Valid2), .DirtyOut(Dirty2),
    .AgeOut(Age2), .Line2MemOut(Line2MemOut2));
  // Probe on OutAge0
  // Probe on OutAge1
  // Probe on OutAge2
  // Probe on ByteRead0
  // Probe on ByteRead2
  Comparator #(.mode("unsigned"), .width(2)) comparator_1 (.a(Age0), .b(2'b10), .eq(Is0eldest));  // open: gt, lt
  Comparator #(.mode("unsigned"), .width(2)) comparator_2 (.a(Age1), .b(2'b10), .eq(Is1eldest));  // open: gt, lt
  Comparator #(.mode("unsigned"), .width(2)) comparator_3 (.a(Age2), .b(2'b10), .eq(Is2eldest));  // open: gt, lt
  // Probe on Index
  BitFinder #(.width(3)) bitfinder_1 (.in({Contain2, Contain1, Contain0}), .index(Index), .found(Contains));
  Comparator #(.width(2)) comparator_4 (.a(Age0), .b(2'b00), .eq(comparator_4_eq));  // open: gt, lt
  Comparator #(.width(2)) comparator_5 (.a(Age1), .b(2'b00), .eq(comparator_5_eq));  // open: gt, lt
  Comparator #(.width(2)) comparator_6 (.a(Age2), .b(2'b00), .eq(comparator_6_eq));  // open: gt, lt
  and and_1 (and_1_out, comparator_4_eq, comparator_5_eq, comparator_6_eq);
  Multiplexer #(.enable("false"), .width(2)) multiplexer_1 (
    .in0(2'b10), .in1(2'b10), .out(multiplexer_1_out), .sel(Is2eldest));
  Multiplexer #(.enable("false"), .width(2)) multiplexer_2 (
    .in0(OutAge0), .in1(2'b00), .out(NewOutAge0), .sel(and_1_out));
  Multiplexer #(.enable("false"), .width(2)) multiplexer_3 (
    .in0(OutAge2), .in1(2'b10), .out(NewOutAge2), .sel(and_1_out));
  Multiplexer #(.enable("false"), .width(2)) multiplexer_4 (
    .in0(multiplexer_1_out), .in1(2'b01), .out(multiplexer_4_out), .sel(Is1eldest));
  Demultiplexer #(.enable("false"), .select(2)) demultiplexer_1 (
    .out0(Byte0), .out1(Byte1), .out2(Byte2), .in(Byte), .sel(Selecting));  // open: out3
  Demultiplexer #(.enable("false"), .select(2)) demultiplexer_2 (
    .out0(Way0), .out1(Way1), .out2(Way2), .in(Ways), .sel(Selecting));  // open: out3
  // Probe on comparator_7_eq[0]
  Comparator #(.mode("unsigned"), .width(2)) comparator_7 (
    .a(NewOutAge0), .b(2'b10), .eq(comparator_7_eq[0]));  // open: gt, lt
  Comparator #(.mode("unsigned"), .width(2)) comparator_8 (
    .a(NewOutAge1), .b(2'b10), .eq(comparator_7_eq[1]));  // open: gt, lt
  Comparator #(.mode("unsigned"), .width(2)) comparator_9 (
    .a(NewOutAge2), .b(2'b10), .eq(comparator_7_eq[2]));  // open: gt, lt
  Multiplexer #(.enable("false"), .width(2)) multiplexer_5 (
    .in0(multiplexer_4_out), .in1(2'b00), .out(multiplexer_5_out), .sel(Is0eldest));
  BitFinder #(.width(3)) bitfinder_2 (.in(comparator_7_eq), .index(bitfinder_2_index));  // open: found
  Multiplexer #(.enable("false"), .width(2)) multiplexer_6 (
    .in0(OutAge1), .in1(2'b01), .out(NewOutAge1), .sel(and_1_out));
  // Probe on ByteRead1
  Way u_Way1 (
    .LineFromMemIn(LineFromMemIn), .CpuAddressOut(CpuAddressOut), .CpuWriteValueIn(CpuWriteValueIn),
    .Initialize(Initialize), .NewAge(Ages), .Line(Way1), .Byte(Byte1), .Age(SelectAge), .ClkIn(ClkIn),
    .Contains(Contain1), .ByteReadOut(ByteRead1), .TagOut(Tag1), .ValidOut(Valid1), .DirtyOut(Dirty1),
    .AgeOut(Age1), .Line2MemOut(Line2Mem));
  // Probe on bitfinder_2_index
  Multiplexer #(.enable("false"), .width(2)) multiplexer_7 (
    .in0(bitfinder_2_index), .in1(2'b10), .out(multiplexer_7_out), .sel(Contain2));
  Multiplexer #(.enable("false"), .width(2)) multiplexer_8 (
    .in0(multiplexer_7_out), .in1(2'b01), .out(multiplexer_8_out), .sel(Contain1));
  Multiplexer #(.enable("false"), .select(2)) multiplexer_9 (
    .in0(Dirty0), .in1(Dirty1), .in2(Dirty2), .out(Dirty), .sel(Selecting));  // open: in3
  Multiplexer #(.enable("false"), .select(2), .width(8)) multiplexer_10 (
    .in0(ByteRead0), .in1(ByteRead1), .in2(ByteRead2), .out(ByteReadOut), .sel(Index));  // open: in3
  Multiplexer #(.enable("false"), .select(2), .width(7)) multiplexer_11 (
    .in0(Tag0), .in1(Tag1), .in2(Tag2), .out(Tag), .sel(Selecting));  // open: in3
  Multiplexer #(.enable("false"), .select(2), .width(32)) multiplexer_12 (
    .in0(Line2MemOut0), .in1(Line2Mem), .in2(Line2MemOut2), .out(Line2Mem), .sel(Selecting));  // open: in3
  Multiplexer #(.enable("false"), .select(2), .width(2)) multiplexer_13 (
    .in0(Age0), .in1(Age1), .in2(Age2), .out(SelectAge), .sel(Selecting));  // open: in3
  Multiplexer #(.enable("false"), .width(2)) multiplexer_14 (
    .in0(multiplexer_8_out), .in1(2'b00), .out(Selecting), .sel(Contain0));
  // Probe on Selecting

  // Other names for the same wires on the sheet: ByteRead[7:0] = ByteReadOut; clk = ClkIn;
  //   CpuWriteValue[7:0] = CpuWriteValueIn; Line2MemOut1[31:0] = Line2Mem; LineFromMem[31:0] = LineFromMemIn
endmodule

module Way (
  input  [31:0] LineFromMemIn,
  input  [9:0] CpuAddressOut,
  input  [7:0] CpuWriteValueIn,
  input  Initialize,
  input  NewAge,
  input  Line,
  input  Byte,
  input  [1:0] Age,
  input  ClkIn,
  output Contains,
  output [7:0] ByteReadOut,
  output [6:0] TagOut,
  output ValidOut,
  output DirtyOut,
  output [1:0] AgeOut,
  output [31:0] Line2MemOut
);

  wire and_1_out, Byte0, Byte1, Byte2, Byte3, comparator_1_eq, not_1_out, or_1_out, or_2_out, or_3_out,
       or_4_out, or_5_out, or_6_out;
  wire [7:0] multiplexer_1_out, multiplexer_2_out, multiplexer_3_out, multiplexer_4_out;

  Demultiplexer #(.enable("false"), .select(2)) demultiplexer_1 (
    .out0(Byte0), .out1(Byte1), .out2(Byte2), .out3(Byte3), .in(Byte), .sel(CpuAddressOut[1:0]));
  Register #(.width(7)) Tag (.D(CpuAddressOut[9:3]), .en(Line), .clk(ClkIn), .Q(TagOut));  // open: clr
  Register #(.width(1)) Valid (.D(Line), .en(Line), .clk(ClkIn), .Q(ValidOut));  // open: clr
  not not_1 (not_1_out, Line);
  or or_1 (or_1_out, not_1_out, Byte);
  or or_2 (or_2_out, Line, Byte);
  and and_1 (and_1_out, NewAge, Initialize);
  // Probe on TagOut
  Register #(.width(1)) register_1 (.D(or_1_out), .en(or_2_out), .clk(ClkIn), .Q(DirtyOut));  // open: clr
  Register #(.width(2)) register_2 (.D(Age), .en(and_1_out), .clk(ClkIn), .Q(AgeOut));  // open: clr
  // Probe on CpuAddressOut[9:3]
  Comparator #(.width(7)) comparator_1 (.a(CpuAddressOut[9:3]), .b(TagOut), .eq(comparator_1_eq));  // open: gt, lt
  and and_2 (Contains, comparator_1_eq, ValidOut);
  Multiplexer #(.enable("false"), .width(8)) multiplexer_1 (
    .in0(LineFromMemIn[7:0]), .in1(CpuWriteValueIn), .out(multiplexer_1_out), .sel(Byte));
  Multiplexer #(.enable("false"), .width(8)) multiplexer_2 (
    .in0(LineFromMemIn[15:8]), .in1(CpuWriteValueIn), .out(multiplexer_2_out), .sel(Byte));
  Multiplexer #(.enable("false"), .width(8)) multiplexer_3 (
    .in0(LineFromMemIn[23:16]), .in1(CpuWriteValueIn), .out(multiplexer_3_out), .sel(Byte));
  Multiplexer #(.enable("false"), .width(8)) multiplexer_4 (
    .in0(LineFromMemIn[31:24]), .in1(CpuWriteValueIn), .out(multiplexer_4_out), .sel(Byte));
  or or_3 (or_3_out, Byte0, Line);
  or or_4 (or_4_out, Byte1, Line);
  or or_5 (or_5_out, Byte2, Line);
  or or_6 (or_6_out, Byte3, Line);
  Register register_3 (.D(multiplexer_1_out), .en(or_3_out), .clk(ClkIn), .Q(Line2MemOut[7:0]));  // open: clr
  Register register_4 (.D(multiplexer_2_out), .en(or_4_out), .clk(ClkIn), .Q(Line2MemOut[15:8]));  // open: clr
  Register register_5 (.D(multiplexer_3_out), .en(or_5_out), .clk(ClkIn), .Q(Line2MemOut[23:16]));  // open: clr
  Register register_6 (.D(multiplexer_4_out), .en(or_6_out), .clk(ClkIn), .Q(Line2MemOut[31:24]));  // open: clr
  // Probe on Line2MemOut[7:0]
  // Probe on Line2MemOut[15:8]
  // Probe on Line2MemOut[23:16]
  // Probe on Line2MemOut[31:24]
  Multiplexer #(.enable("false"), .select(2), .width(8)) multiplexer_5 (
    .in0(Line2MemOut[7:0]), .in1(Line2MemOut[15:8]), .in2(Line2MemOut[23:16]), .in3(Line2MemOut[31:24]),
    .out(ByteReadOut), .sel(CpuAddressOut[1:0]));
  // Probe on ByteReadOut

  // Other names for the same wires on the sheet: clk = ClkIn; OffSet[1:0] = CpuAddressOut[1:0];
  //   Sets = CpuAddressOut[2]; Tag[6:0] = CpuAddressOut[9:3]; CpuWriteValue[7:0] = CpuWriteValueIn;
  //   LineFromMem[31:0] = LineFromMemIn
endmodule

module Controlpath (
  input  [9:0] CpuAddressIn,
  input  CpuRead,
  input  CpuWrite,
  input  Dirty,
  input  Contain,
  input  ClkIn,
  output [9:0] CpuAddressOut,
  output Initialize,
  output MemWrite,
  output MemRead,
  output Age0,
  output Age1,
  output Line0,
  output Line1,
  output Byte0,
  output Byte1,
  output Ready,
  output NewContain
);

  wire fsm_1_age, fsm_1_line, fsm_1_update, or_1_out, or_2_out, OutRead, OutWrite, Read, State, Write, Yes;
  wire [2:0] fsm_1_out0, register_1_q;
  wire [7:0] CpuWriteValue, WriteValue;

  FSM fsm_1 (
    .S0(register_1_q[0]), .S1(register_1_q[1]), .S2(register_1_q[2]), .Read(Read), .Write(Write),
    .Contain(Contain), .Dirty(Dirty), .Out0(fsm_1_out0[0]), .Out1(fsm_1_out0[1]), .Out2(fsm_1_out0[2]),
    .Ready(Ready), .MemWrite(MemWrite), .MemRead(MemRead), .Age(fsm_1_age), .Line(fsm_1_line),
    .Update(fsm_1_update), .State(State), .Initialize(Initialize));
  Multiplexer #(.enable("false")) multiplexer_1 (.in0(OutRead), .in1(CpuRead), .out(Read), .sel(Ready));
  Multiplexer #(.enable("false")) multiplexer_2 (.in0(OutWrite), .in1(CpuWrite), .out(Write), .sel(Ready));
  Demultiplexer #(.enable("false")) demultiplexer_1 (.out0(Age0), .out1(Age1), .in(fsm_1_age), .sel(CpuAddressOut[2]));
  Demultiplexer #(.enable("false")) demultiplexer_2 (
    .out0(Line0), .out1(Line1), .in(fsm_1_line), .sel(CpuAddressOut[2]));
  Demultiplexer #(.enable("false")) demultiplexer_3 (
    .out0(Byte0), .out1(Byte1), .in(fsm_1_update), .sel(CpuAddressOut[2]));
  and and_1 (Yes, Ready, or_1_out);
  or or_1 (or_1_out, CpuRead, CpuWrite);
  Register #(.width(3)) register_1 (.D(fsm_1_out0), .en(1'b1), .clk(ClkIn), .Q(register_1_q));  // open: clr
  Register #(.width(10)) register_2 (.D(CpuAddressIn), .en(Ready), .clk(ClkIn), .Q(CpuAddressOut));  // open: clr
  Register #(.width(1)) register_3 (.D(CpuRead), .en(Yes), .clk(ClkIn), .Q(OutRead));  // open: clr
  Register #(.width(1)) register_4 (.D(CpuWrite), .en(Yes), .clk(ClkIn), .Q(OutWrite));  // open: clr
  // Probe on CpuAddressOut
  Register register_5 (.D(CpuWriteValue), .en(Yes), .clk(ClkIn), .Q(WriteValue));  // open: clr
  or or_2 (or_2_out, OutRead, OutWrite);
  and and_2 (NewContain, State, or_2_out);

  // Other names for the same wires on the sheet: Clk = ClkIn; CpuAddress[9:0] = CpuAddressIn;
  //   Offset[1:0] = CpuAddressOut[1:0]; Sets = CpuAddressOut[2]; Tag[6:0] = CpuAddressOut[9:3]
endmodule
